// Logisim project Md.SayadulHaque-1421353042.circ as structural Verilog: 1 circuit, main circuit main
module main (
  input  C3,
  input  [3:0] C2,
  input  A0,
  input  A1,
  input  A2,
  input  C1,
  input  B0,
  input  B1,
  input  B2,
  output [2:0] B,
  output [2:0] A,
  output [3:0] Sum,
  output Carry,
  output out_14,
  output out_15,
  output out_16,
  output out_17,
  output [3:0] Result
);

  wire adder_1_cout, adder_2_cout, comparator_1_eq, comparator_1_gt, comparator_1_lt, or_1_out, xor_2_out,
       xor_3_out, xor_4_out;
  wire [3:0] bit_extender_1_out, bit_extender_2_out, xor_1_out, xor_5_out;

  assign bit_extender_1_out = {{1{1'b0}}, {A2, A1, A0}};  // Bit_Extender bit_extender_1
  assign xor_1_out = bit_extender_2_out ^ bit_extender_1_out;  // XOR_Gate xor_1, 4 bits wide
  LED A__B (.in(or_1_out));
  assign bit_extender_2_out = {{1{1'b0}}, {B2, B1, B0}};  // Bit_Extender bit_extender_2
  LED A_B (.in(comparator_1_lt));
  Comparator #(.width(3), .mode("unsigned")) comparator_1 (
    .a({A2, A1, A0}), .b({B2, B1, B0}), .gt(comparator_1_gt), .eq(comparator_1_eq), .lt(comparator_1_lt));
  or or_1 (or_1_out, comparator_1_gt, comparator_1_eq);
  xor xor_2 (xor_2_out, B0, C1);
  Adder #(.width(1)) adder_1 (.a(xor_2_out), .b(A0), .out(out_14), .cin(C1), .cout(adder_1_cout));
  Multiplexer #(.width(4)) multiplexer_1 (.in0(xor_1_out), .in1(Sum), .out(Result), .sel(or_1_out), .en(1'b1));
  xor xor_3 (xor_3_out, B1, C1);
  Adder #(.width(1)) adder_2 (.a(xor_3_out), .b(A1), .out(out_15), .cin(adder_1_cout), .cout(adder_2_cout));
  xor xor_4 (xor_4_out, B2, C1);
  Adder #(.width(1)) adder_3 (.a(xor_4_out), .b(A2), .out(out_16), .cin(adder_2_cout), .cout(out_17));
  assign xor_5_out = C2 ^ 4'b0001;  // XOR_Gate xor_5, 4 bits wide
  Adder #(.width(4)) adder_4 (.a(xor_5_out), .b({out_17, out_16, out_15, out_14}), .out(Sum), .cin(C3), .cout(Carry));

  assign A = {A2, A1, A0};
  assign B = {B2, B1, B0};

  // Notes on the sheet:
  //   Input A
  //   Input B
endmodule
